// Logisim project ALU_4BIT.circ as structural Verilog: 1 circuit, main circuit ALU_4BIT
module ALU_4BIT (
  input  [3:0] A,
  input  [3:0] B,
  input  [3:0] in_3,
  input  [3:0] OPCODE,
  output [3:0] ADD_RESULT,
  output [3:0] SUB_RESULT,
  output [3:0] AND_RESULT,
  output [3:0] OR_RESULT,
  output [3:0] RESULT,
  output [3:0] XOR_RESULT,
  output [3:0] NOT_RESULT,
  output out_12,
  output out_13,
  output Z,
  output out_15,
  output [3:0] GT_RESULT,
  output [3:0] EQ_RESULT,
  output C,
  output [3:0] LT_RESULT
);

  wire adder_1_cout, not_2_out, subtractor_1_bout;

  Comparator #(.width(4)) comparator_1 (.a(A), .b(B), .gt(out_12), .eq(out_13), .lt(out_15));
  Adder #(.width(4)) adder_1 (.a(A), .b(B), .out(ADD_RESULT), .cin(1'b0), .cout(adder_1_cout));
  Subtractor #(.width(4)) subtractor_1 (.a(A), .b(B), .out(SUB_RESULT), .bin(1'b0), .bout(subtractor_1_bout));
  assign AND_RESULT = A & B;  // AND_Gate and_1, 4 bits wide
  assign OR_RESULT = A | B;  // OR_Gate or_1, 4 bits wide
  assign XOR_RESULT = A ^ B;  // XOR_Gate xor_1, 4 bits wide
  assign NOT_RESULT = ~A;  // NOT_Gate not_1, 4 bits wide
  Multiplexer #(.width(4)) multiplexer_1 (.in0(4'b0000), .in1(4'b0001), .out(GT_RESULT), .sel(out_12));  // open: en
  Multiplexer #(.width(4)) multiplexer_2 (.in0(4'b0000), .in1(4'b0001), .out(EQ_RESULT), .sel(out_13));  // open: en
  Multiplexer #(.width(4)) multiplexer_3 (.in0(4'b0000), .in1(4'b0001), .out(LT_RESULT), .sel(out_15));  // open: en
  Multiplexer #(.select(4), .width(4)) multiplexer_4 (
    .in0(ADD_RESULT), .in1(SUB_RESULT), .in2(AND_RESULT), .in3(OR_RESULT), .in4(XOR_RESULT),
    .in5(NOT_RESULT), .in6(GT_RESULT), .in7(EQ_RESULT), .in8(LT_RESULT), .in9(in_3), .in10(in_3),
    .in11(in_3), .in12(in_3), .in13(in_3), .in14(in_3), .in15(in_3), .out(RESULT), .sel(OPCODE));  // open: en
  Multiplexer multiplexer_5 (.in0(adder_1_cout), .in1(not_2_out), .out(C), .sel(OPCODE[0]));  // open: en
  not not_2 (not_2_out, subtractor_1_bout);
  Comparator #(.width(4)) comparator_2 (.a(RESULT), .b(4'b0000), .eq(Z));  // open: gt, lt
endmodule
